// Logisim project 8bit_computer.circ as structural Verilog: 1 circuit, main circuit main
module main (
);

  wire and_1_out, and_2_out, and_3_out, and_4_out, and_5_out, and_6_out, and_7_out, and_8_out, and_9_out,
       and_10_out, and_11_out, and_12_out, and_13_out, and_14_out, and_15_out, and_16_out, and_17_out,
       and_18_out, and_19_out, and_20_out, and_21_out, and_22_out, and_23_out, and_24_out, and_25_out,
       and_26_out, and_27_out, and_28_out, and_29_out, and_30_out, and_31_out, and_32_out, and_33_out,
       and_34_out, and_35_out, and_36_out, and_37_out, and_38_out, and_39_out, and_40_out, and_41_out,
       and_42_out, and_43_out, and_44_out, and_45_out, and_46_out, and_47_out, and_48_out, and_49_out,
       and_50_out, and_51_out, and_52_out, and_53_out, and_54_out, and_55_out, and_56_out, and_57_out,
       and_58_out, and_59_out, and_60_out, and_61_out, and_62_out, and_63_out, and_64_out, and_65_out,
       and_66_out, and_67_out, and_68_out, and_69_out, and_70_out, and_71_out, and_72_out, and_73_out,
       and_74_out, and_75_out, and_76_out, and_77_out, and_78_out, and_79_out, and_80_out, and_81_out,
       and_82_out, and_83_out, and_84_out, and_85_out, and_86_out, and_87_out, and_88_out, and_89_out,
       and_90_out, and_91_out, and_92_out, and_93_out, and_94_out, and_95_out, and_96_out, and_97_out,
       and_98_out, and_99_out, and_100_out, and_101_out, and_102_out, and_103_out, and_104_out, and_105_out,
       and_106_out, and_107_out, and_108_out, and_109_out, and_110_out, and_111_out, and_112_out,
       and_113_out, and_114_out, and_115_out, and_116_out, and_117_out, and_118_out, and_119_out,
       and_120_out, and_121_out, and_122_out, and_123_out, and_124_out, and_125_out, and_126_out,
       and_127_out, and_128_out, and_129_out, and_130_out, and_131_out, and_132_out, and_133_out,
       and_134_out, and_135_out, and_136_out, and_137_out, and_138_out, and_139_out, and_140_out,
       and_141_out, and_142_out, and_143_out, and_144_out, and_145_out, and_146_out, and_147_out,
       and_148_out, and_149_out, and_150_out, and_151_out, and_152_out, and_153_out, and_154_out,
       and_155_out, and_156_out, and_157_out, and_158_out, and_159_out, and_160_out, and_161_out,
       and_162_out, and_163_out, and_164_out, and_165_out, and_166_out, and_167_out, and_168_out,
       and_169_out, and_170_out, and_171_out, and_172_out, and_173_out, and_174_out, and_175_out, or_1_out,
       or_2_out, or_3_out, or_4_out, or_5_out, or_6_out, or_7_out, s_r_ff_1_q, s_r_ff_2_q, s_r_ff_3_q,
       s_r_ff_4_q, s_r_ff_5_q, s_r_ff_6_q, s_r_ff_7_q, s_r_ff_8_q, s_r_ff_9_q, s_r_ff_10_q, s_r_ff_11_q,
       s_r_ff_12_q, s_r_ff_13_q, s_r_ff_14_q, s_r_ff_15_q, s_r_ff_16_q, undriven, undriven_2, undriven_3,
       undriven_4, undriven_5, undriven_6, undriven_7, undriven_8, undriven_9, undriven_10, undriven_11,
       undriven_12, undriven_13, undriven_14, undriven_15, undriven_16, undriven_17, undriven_18,
       undriven_19, undriven_20, xor_1_out, xor_2_out, xor_3_out, xor_4_out, xor_5_out, xor_6_out, xor_7_out,
       xor_8_out, xor_9_out, xor_10_out, xor_11_out, xor_12_out, xor_13_out, xor_14_out, xor_15_out;

  and and_1 (and_1_out, or_1_out, undriven_3);
  and and_2 (and_2_out, undriven_3, undriven);
  S_R_Flip_Flop s_r_ff_1 (.Q(s_r_ff_1_q), .reset(and_2_out), .preset(and_1_out));  // open: S, R, clk, Qn
  and and_3 (and_3_out, or_1_out, undriven_4);
  and and_4 (and_4_out, undriven_4, undriven_2);
  S_R_Flip_Flop s_r_ff_2 (.Q(s_r_ff_2_q), .reset(and_4_out), .preset(and_3_out));  // open: S, R, clk, Qn
  xor xor_1 (xor_1_out, s_r_ff_1_q, s_r_ff_2_q);
  and and_5 (and_5_out, xor_4_out, undriven_3);
  and and_6 (and_6_out, undriven_3, undriven);
  and and_7 (and_7_out, xor_4_out, undriven_4);
  and and_8 (and_8_out, undriven_4, undriven_2);
  xor xor_2 (xor_2_out, xor_1_out, or_2_out);
  S_R_Flip_Flop s_r_ff_3 (.Q(s_r_ff_3_q), .reset(and_6_out), .preset(and_5_out));  // open: S, R, clk, Qn
  S_R_Flip_Flop s_r_ff_4 (.Q(s_r_ff_4_q), .reset(and_8_out), .preset(and_7_out));  // open: S, R, clk, Qn
  and and_9 (and_9_out, xor_1_out, or_2_out);
  or or_1 (or_1_out, and_9_out, and_10_out);
  and and_10 (and_10_out, s_r_ff_1_q, s_r_ff_2_q);
  xor xor_3 (xor_3_out, s_r_ff_3_q, s_r_ff_4_q);
  xor xor_4 (xor_4_out, xor_3_out, or_3_out);
  and and_11 (and_11_out, xor_6_out, undriven_3);
  and and_12 (and_12_out, undriven_3, undriven);
  and and_13 (and_13_out, xor_6_out, undriven_4);
  and and_14 (and_14_out, undriven_4, undriven_2);
  and and_15 (and_15_out, xor_3_out, or_3_out);
  S_R_Flip_Flop s_r_ff_5 (.Q(s_r_ff_5_q), .reset(and_12_out), .preset(and_11_out));  // open: S, R, clk, Qn
  S_R_Flip_Flop s_r_ff_6 (.Q(s_r_ff_6_q), .reset(and_14_out), .preset(and_13_out));  // open: S, R, clk, Qn
  or or_2 (or_2_out, and_15_out, and_16_out);
  and and_16 (and_16_out, s_r_ff_3_q, s_r_ff_4_q);
  xor xor_5 (xor_5_out, s_r_ff_5_q, s_r_ff_6_q);
  xor xor_6 (xor_6_out, xor_5_out, or_4_out);
  and and_17 (and_17_out, xor_8_out, undriven_3);
  and and_18 (and_18_out, undriven_3, undriven);
  and and_19 (and_19_out, xor_8_out, undriven_4);
  and and_20 (and_20_out, undriven_4, undriven_2);
  or or_3 (or_3_out, and_21_out, and_22_out);
  and and_21 (and_21_out, xor_5_out, or_4_out);
  and and_22 (and_22_out, s_r_ff_5_q, s_r_ff_6_q);
  S_R_Flip_Flop s_r_ff_7 (.Q(s_r_ff_7_q), .reset(and_18_out), .preset(and_17_out));  // open: S, R, clk, Qn
  S_R_Flip_Flop s_r_ff_8 (.Q(s_r_ff_8_q), .reset(and_20_out), .preset(and_19_out));  // open: S, R, clk, Qn
  xor xor_7 (xor_7_out, s_r_ff_7_q, s_r_ff_8_q);
  xor xor_8 (xor_8_out, xor_7_out, or_5_out);
  and and_23 (and_23_out, xor_7_out, or_5_out);
  and and_24 (and_24_out, xor_10_out, undriven_3);
  and and_25 (and_25_out, undriven_3, undriven);
  or or_4 (or_4_out, and_23_out, and_26_out);
  and and_26 (and_26_out, s_r_ff_7_q, s_r_ff_8_q);
  S_R_Flip_Flop s_r_ff_9 (.Q(s_r_ff_9_q), .reset(and_25_out), .preset(and_24_out));  // open: S, R, clk, Qn
  and and_27 (and_27_out, xor_10_out, undriven_4);
  and and_28 (and_28_out, undriven_4, undriven_2);
  xor xor_9 (xor_9_out, s_r_ff_9_q, s_r_ff_10_q);
  S_R_Flip_Flop s_r_ff_10 (.Q(s_r_ff_10_q), .reset(and_28_out), .preset(and_27_out));  // open: S, R, clk, Qn
  xor xor_10 (xor_10_out, xor_9_out, or_6_out);
  and and_29 (and_29_out, xor_9_out, or_6_out);
  or or_5 (or_5_out, and_29_out, and_30_out);
  and and_30 (and_30_out, s_r_ff_9_q, s_r_ff_10_q);
  xor xor_11 (xor_11_out, s_r_ff_11_q, s_r_ff_12_q);
  and and_31 (and_31_out, xor_12_out, undriven_3);
  and and_32 (and_32_out, undriven_3, undriven);
  and and_33 (and_33_out, xor_12_out, undriven_4);
  and and_34 (and_34_out, undriven_4, undriven_2);
  S_R_Flip_Flop s_r_ff_11 (.Q(s_r_ff_11_q), .reset(and_32_out), .preset(and_31_out));  // open: S, R, clk, Qn
  S_R_Flip_Flop s_r_ff_12 (.Q(s_r_ff_12_q), .reset(and_34_out), .preset(and_33_out));  // open: S, R, clk, Qn
  xor xor_12 (xor_12_out, xor_11_out, or_7_out);
  or or_6 (or_6_out, and_35_out, and_36_out);
  and and_35 (and_35_out, xor_11_out, or_7_out);
  and and_36 (and_36_out, s_r_ff_11_q, s_r_ff_12_q);
  xor xor_13 (xor_13_out, s_r_ff_13_q, s_r_ff_14_q);
  and and_37 (and_37_out, xor_14_out, undriven_3);
  and and_38 (and_38_out, undriven_3, undriven);
  and and_39 (and_39_out, xor_14_out, undriven_4);
  and and_40 (and_40_out, undriven_4, undriven_2);
  xor xor_14 (xor_14_out, xor_13_out, and_43_out);
  S_R_Flip_Flop s_r_ff_13 (.Q(s_r_ff_13_q), .reset(and_38_out), .preset(and_37_out));  // open: S, R, clk, Qn
  S_R_Flip_Flop s_r_ff_14 (.Q(s_r_ff_14_q), .reset(and_40_out), .preset(and_39_out));  // open: S, R, clk, Qn
  or or_7 (or_7_out, and_41_out, and_42_out);
  and and_41 (and_41_out, xor_13_out, and_43_out);
  and and_42 (and_42_out, s_r_ff_13_q, s_r_ff_14_q);
  xor xor_15 (xor_15_out, s_r_ff_15_q, s_r_ff_16_q);
  and and_43 (and_43_out, s_r_ff_15_q, s_r_ff_16_q);
  and and_44 (and_44_out, xor_15_out, undriven_3);
  and and_45 (and_45_out, undriven_3, undriven);
  and and_46 (and_46_out, xor_15_out, undriven_4);
  and and_47 (and_47_out, undriven_4, undriven_2);
  S_R_Flip_Flop s_r_ff_15 (.Q(s_r_ff_15_q), .reset(and_45_out), .preset(and_44_out));  // open: S, R, clk, Qn
  S_R_Flip_Flop s_r_ff_16 (.Q(s_r_ff_16_q), .reset(and_47_out), .preset(and_46_out));  // open: S, R, clk, Qn
  and and_48 (and_48_out, xor_15_out, undriven_13);
  and and_49 (and_49_out, undriven_13, undriven_5);
  and and_50 (and_50_out, xor_15_out, undriven_14);
  and and_51 (and_51_out, undriven_14, undriven_6);
  and and_52 (and_52_out, xor_15_out, undriven_15);
  and and_53 (and_53_out, undriven_15, undriven_7);
  and and_54 (and_54_out, xor_15_out, undriven_16);
  and and_55 (and_55_out, undriven_16, undriven_8);
  and and_56 (and_56_out, xor_15_out, undriven_17);
  and and_57 (and_57_out, undriven_17, undriven_9);
  and and_58 (and_58_out, xor_15_out, undriven_18);
  and and_59 (and_59_out, undriven_18, undriven_10);
  and and_60 (and_60_out, xor_15_out, undriven_19);
  and and_61 (and_61_out, undriven_19, undriven_11);
  and and_62 (and_62_out, xor_15_out, undriven_20);
  and and_63 (and_63_out, undriven_20, undriven_12);
  S_R_Flip_Flop s_r_ff_17 (.Q(xor_15_out), .reset(and_49_out), .preset(and_48_out));  // open: S, R, clk, Qn
  S_R_Flip_Flop s_r_ff_18 (.Q(xor_15_out), .reset(and_51_out), .preset(and_50_out));  // open: S, R, clk, Qn
  S_R_Flip_Flop s_r_ff_19 (.Q(xor_15_out), .reset(and_53_out), .preset(and_52_out));  // open: S, R, clk, Qn
  S_R_Flip_Flop s_r_ff_20 (.Q(xor_15_out), .reset(and_55_out), .preset(and_54_out));  // open: S, R, clk, Qn
  S_R_Flip_Flop s_r_ff_21 (.Q(xor_15_out), .reset(and_57_out), .preset(and_56_out));  // open: S, R, clk, Qn
  S_R_Flip_Flop s_r_ff_22 (.Q(xor_15_out), .reset(and_59_out), .preset(and_58_out));  // open: S, R, clk, Qn
  S_R_Flip_Flop s_r_ff_23 (.Q(xor_15_out), .reset(and_61_out), .preset(and_60_out));  // open: S, R, clk, Qn
  S_R_Flip_Flop s_r_ff_24 (.Q(xor_15_out), .reset(and_63_out), .preset(and_62_out));  // open: S, R, clk, Qn
  and and_64 (and_64_out, xor_14_out, undriven_13);
  and and_65 (and_65_out, undriven_13, undriven_5);
  and and_66 (and_66_out, xor_14_out, undriven_14);
  and and_67 (and_67_out, undriven_14, undriven_6);
  and and_68 (and_68_out, xor_14_out, undriven_15);
  and and_69 (and_69_out, undriven_15, undriven_7);
  and and_70 (and_70_out, xor_14_out, undriven_16);
  and and_71 (and_71_out, undriven_16, undriven_8);
  and and_72 (and_72_out, xor_14_out, undriven_17);
  and and_73 (and_73_out, undriven_17, undriven_9);
  and and_74 (and_74_out, xor_14_out, undriven_18);
  and and_75 (and_75_out, undriven_18, undriven_10);
  and and_76 (and_76_out, xor_14_out, undriven_19);
  and and_77 (and_77_out, undriven_19, undriven_11);
  and and_78 (and_78_out, xor_14_out, undriven_20);
  and and_79 (and_79_out, undriven_20, undriven_12);
  S_R_Flip_Flop s_r_ff_25 (.Q(xor_14_out), .reset(and_65_out), .preset(and_64_out));  // open: S, R, clk, Qn
  S_R_Flip_Flop s_r_ff_26 (.Q(xor_14_out), .reset(and_67_out), .preset(and_66_out));  // open: S, R, clk, Qn
  S_R_Flip_Flop s_r_ff_27 (.Q(xor_14_out), .reset(and_69_out), .preset(and_68_out));  // open: S, R, clk, Qn
  S_R_Flip_Flop s_r_ff_28 (.Q(xor_14_out), .reset(and_71_out), .preset(and_70_out));  // open: S, R, clk, Qn
  S_R_Flip_Flop s_r_ff_29 (.Q(xor_14_out), .reset(and_73_out), .preset(and_72_out));  // open: S, R, clk, Qn
  S_R_Flip_Flop s_r_ff_30 (.Q(xor_14_out), .reset(and_75_out), .preset(and_74_out));  // open: S, R, clk, Qn
  S_R_Flip_Flop s_r_ff_31 (.Q(xor_14_out), .reset(and_77_out), .preset(and_76_out));  // open: S, R, clk, Qn
  S_R_Flip_Flop s_r_ff_32 (.Q(xor_14_out), .reset(and_79_out), .preset(and_78_out));  // open: S, R, clk, Qn
  and and_80 (and_80_out, xor_12_out, undriven_13);
  and and_81 (and_81_out, undriven_13, undriven_5);
  and and_82 (and_82_out, xor_12_out, undriven_14);
  and and_83 (and_83_out, undriven_14, undriven_6);
  and and_84 (and_84_out, xor_12_out, undriven_15);
  and and_85 (and_85_out, undriven_15, undriven_7);
  and and_86 (and_86_out, xor_12_out, undriven_16);
  and and_87 (and_87_out, undriven_16, undriven_8);
  and and_88 (and_88_out, xor_12_out, undriven_17);
  and and_89 (and_89_out, undriven_17, undriven_9);
  and and_90 (and_90_out, xor_12_out, undriven_18);
  and and_91 (and_91_out, undriven_18, undriven_10);
  and and_92 (and_92_out, xor_12_out, undriven_19);
  and and_93 (and_93_out, undriven_19, undriven_11);
  and and_94 (and_94_out, xor_12_out, undriven_20);
  and and_95 (and_95_out, undriven_20, undriven_12);
  S_R_Flip_Flop s_r_ff_33 (.Q(xor_12_out), .reset(and_81_out), .preset(and_80_out));  // open: S, R, clk, Qn
  S_R_Flip_Flop s_r_ff_34 (.Q(xor_12_out), .reset(and_83_out), .preset(and_82_out));  // open: S, R, clk, Qn
  S_R_Flip_Flop s_r_ff_35 (.Q(xor_12_out), .reset(and_85_out), .preset(and_84_out));  // open: S, R, clk, Qn
  S_R_Flip_Flop s_r_ff_36 (.Q(xor_12_out), .reset(and_87_out), .preset(and_86_out));  // open: S, R, clk, Qn
  S_R_Flip_Flop s_r_ff_37 (.Q(xor_12_out), .reset(and_89_out), .preset(and_88_out));  // open: S, R, clk, Qn
  S_R_Flip_Flop s_r_ff_38 (.Q(xor_12_out), .reset(and_91_out), .preset(and_90_out));  // open: S, R, clk, Qn
  S_R_Flip_Flop s_r_ff_39 (.Q(xor_12_out), .reset(and_93_out), .preset(and_92_out));  // open: S, R, clk, Qn
  S_R_Flip_Flop s_r_ff_40 (.Q(xor_12_out), .reset(and_95_out), .preset(and_94_out));  // open: S, R, clk, Qn
  and and_96 (and_96_out, xor_10_out, undriven_13);
  and and_97 (and_97_out, undriven_13, undriven_5);
  and and_98 (and_98_out, xor_10_out, undriven_14);
  and and_99 (and_99_out, undriven_14, undriven_6);
  and and_100 (and_100_out, xor_10_out, undriven_15);
  and and_101 (and_101_out, undriven_15, undriven_7);
  and and_102 (and_102_out, xor_10_out, undriven_16);
  and and_103 (and_103_out, undriven_16, undriven_8);
  and and_104 (and_104_out, xor_10_out, undriven_17);
  and and_105 (and_105_out, undriven_17, undriven_9);
  and and_106 (and_106_out, xor_10_out, undriven_18);
  and and_107 (and_107_out, undriven_18, undriven_10);
  and and_108 (and_108_out, xor_10_out, undriven_19);
  and and_109 (and_109_out, undriven_19, undriven_11);
  and and_110 (and_110_out, xor_10_out, undriven_20);
  and and_111 (and_111_out, undriven_20, undriven_12);
  S_R_Flip_Flop s_r_ff_41 (.Q(xor_10_out), .reset(and_97_out), .preset(and_96_out));  // open: S, R, clk, Qn
  S_R_Flip_Flop s_r_ff_42 (.Q(xor_10_out), .reset(and_99_out), .preset(and_98_out));  // open: S, R, clk, Qn
  S_R_Flip_Flop s_r_ff_43 (.Q(xor_10_out), .reset(and_101_out), .preset(and_100_out));  // open: S, R, clk, Qn
  S_R_Flip_Flop s_r_ff_44 (.Q(xor_10_out), .reset(and_103_out), .preset(and_102_out));  // open: S, R, clk, Qn
  S_R_Flip_Flop s_r_ff_45 (.Q(xor_10_out), .reset(and_105_out), .preset(and_104_out));  // open: S, R, clk, Qn
  S_R_Flip_Flop s_r_ff_46 (.Q(xor_10_out), .reset(and_107_out), .preset(and_106_out));  // open: S, R, clk, Qn
  S_R_Flip_Flop s_r_ff_47 (.Q(xor_10_out), .reset(and_109_out), .preset(and_108_out));  // open: S, R, clk, Qn
  S_R_Flip_Flop s_r_ff_48 (.Q(xor_10_out), .reset(and_111_out), .preset(and_110_out));  // open: S, R, clk, Qn
  and and_112 (and_112_out, xor_8_out, undriven_13);
  and and_113 (and_113_out, undriven_13, undriven_5);
  and and_114 (and_114_out, xor_8_out, undriven_14);
  and and_115 (and_115_out, undriven_14, undriven_6);
  and and_116 (and_116_out, xor_8_out, undriven_15);
  and and_117 (and_117_out, undriven_15, undriven_7);
  and and_118 (and_118_out, xor_8_out, undriven_16);
  and and_119 (and_119_out, undriven_16, undriven_8);
  and and_120 (and_120_out, xor_8_out, undriven_17);
  and and_121 (and_121_out, undriven_17, undriven_9);
  and and_122 (and_122_out, xor_8_out, undriven_18);
  and and_123 (and_123_out, undriven_18, undriven_10);
  and and_124 (and_124_out, xor_8_out, undriven_19);
  and and_125 (and_125_out, undriven_19, undriven_11);
  and and_126 (and_126_out, xor_8_out, undriven_20);
  and and_127 (and_127_out, undriven_20, undriven_12);
  S_R_Flip_Flop s_r_ff_49 (.Q(xor_8_out), .reset(and_113_out), .preset(and_112_out));  // open: S, R, clk, Qn
  S_R_Flip_Flop s_r_ff_50 (.Q(xor_8_out), .reset(and_115_out), .preset(and_114_out));  // open: S, R, clk, Qn
  S_R_Flip_Flop s_r_ff_51 (.Q(xor_8_out), .reset(and_117_out), .preset(and_116_out));  // open: S, R, clk, Qn
  S_R_Flip_Flop s_r_ff_52 (.Q(xor_8_out), .reset(and_119_out), .preset(and_118_out));  // open: S, R, clk, Qn
  S_R_Flip_Flop s_r_ff_53 (.Q(xor_8_out), .reset(and_121_out), .preset(and_120_out));  // open: S, R, clk, Qn
  S_R_Flip_Flop s_r_ff_54 (.Q(xor_8_out), .reset(and_123_out), .preset(and_122_out));  // open: S, R, clk, Qn
  S_R_Flip_Flop s_r_ff_55 (.Q(xor_8_out), .reset(and_125_out), .preset(and_124_out));  // open: S, R, clk, Qn
  S_R_Flip_Flop s_r_ff_56 (.Q(xor_8_out), .reset(and_127_out), .preset(and_126_out));  // open: S, R, clk, Qn
  and and_128 (and_128_out, xor_6_out, undriven_13);
  and and_129 (and_129_out, undriven_13, undriven_5);
  and and_130 (and_130_out, xor_6_out, undriven_14);
  and and_131 (and_131_out, undriven_14, undriven_6);
  and and_132 (and_132_out, xor_6_out, undriven_15);
  and and_133 (and_133_out, undriven_15, undriven_7);
  and and_134 (and_134_out, xor_6_out, undriven_16);
  and and_135 (and_135_out, undriven_16, undriven_8);
  and and_136 (and_136_out, xor_6_out, undriven_17);
  and and_137 (and_137_out, undriven_17, undriven_9);
  and and_138 (and_138_out, xor_6_out, undriven_18);
  and and_139 (and_139_out, undriven_18, undriven_10);
  and and_140 (and_140_out, xor_6_out, undriven_19);
  and and_141 (and_141_out, undriven_19, undriven_11);
  and and_142 (and_142_out, xor_6_out, undriven_20);
  and and_143 (and_143_out, undriven_20, undriven_12);
  S_R_Flip_Flop s_r_ff_57 (.Q(xor_6_out), .reset(and_129_out), .preset(and_128_out));  // open: S, R, clk, Qn
  S_R_Flip_Flop s_r_ff_58 (.Q(xor_6_out), .reset(and_131_out), .preset(and_130_out));  // open: S, R, clk, Qn
  S_R_Flip_Flop s_r_ff_59 (.Q(xor_6_out), .reset(and_133_out), .preset(and_132_out));  // open: S, R, clk, Qn
  S_R_Flip_Flop s_r_ff_60 (.Q(xor_6_out), .reset(and_135_out), .preset(and_134_out));  // open: S, R, clk, Qn
  S_R_Flip_Flop s_r_ff_61 (.Q(xor_6_out), .reset(and_137_out), .preset(and_136_out));  // open: S, R, clk, Qn
  S_R_Flip_Flop s_r_ff_62 (.Q(xor_6_out), .reset(and_139_out), .preset(and_138_out));  // open: S, R, clk, Qn
  S_R_Flip_Flop s_r_ff_63 (.Q(xor_6_out), .reset(and_141_out), .preset(and_140_out));  // open: S, R, clk, Qn
  S_R_Flip_Flop s_r_ff_64 (.Q(xor_6_out), .reset(and_143_out), .preset(and_142_out));  // open: S, R, clk, Qn
  and and_144 (and_144_out, xor_4_out, undriven_13);
  and and_145 (and_145_out, undriven_13, undriven_5);
  and and_146 (and_146_out, xor_4_out, undriven_14);
  and and_147 (and_147_out, undriven_14, undriven_6);
  and and_148 (and_148_out, xor_4_out, undriven_15);
  and and_149 (and_149_out, undriven_15, undriven_7);
  and and_150 (and_150_out, xor_4_out, undriven_16);
  and and_151 (and_151_out, undriven_16, undriven_8);
  and and_152 (and_152_out, xor_4_out, undriven_17);
  and and_153 (and_153_out, undriven_17, undriven_9);
  and and_154 (and_154_out, xor_4_out, undriven_18);
  and and_155 (and_155_out, undriven_18, undriven_10);
  and and_156 (and_156_out, xor_4_out, undriven_19);
  and and_157 (and_157_out, undriven_19, undriven_11);
  and and_158 (and_158_out, xor_4_out, undriven_20);
  and and_159 (and_159_out, undriven_20, undriven_12);
  S_R_Flip_Flop s_r_ff_65 (.Q(xor_4_out), .reset(and_145_out), .preset(and_144_out));  // open: S, R, clk, Qn
  S_R_Flip_Flop s_r_ff_66 (.Q(xor_4_out), .reset(and_147_out), .preset(and_146_out));  // open: S, R, clk, Qn
  S_R_Flip_Flop s_r_ff_67 (.Q(xor_4_out), .reset(and_149_out), .preset(and_148_out));  // open: S, R, clk, Qn
  S_R_Flip_Flop s_r_ff_68 (.Q(xor_4_out), .reset(and_151_out), .preset(and_150_out));  // open: S, R, clk, Qn
  S_R_Flip_Flop s_r_ff_69 (.Q(xor_4_out), .reset(and_153_out), .preset(and_152_out));  // open: S, R, clk, Qn
  S_R_Flip_Flop s_r_ff_70 (.Q(xor_4_out), .reset(and_155_out), .preset(and_154_out));  // open: S, R, clk, Qn
  S_R_Flip_Flop s_r_ff_71 (.Q(xor_4_out), .reset(and_157_out), .preset(and_156_out));  // open: S, R, clk, Qn
  S_R_Flip_Flop s_r_ff_72 (.Q(xor_4_out), .reset(and_159_out), .preset(and_158_out));  // open: S, R, clk, Qn
  and and_160 (and_160_out, or_1_out, undriven_13);
  and and_161 (and_161_out, undriven_13, undriven_5);
  and and_162 (and_162_out, or_1_out, undriven_14);
  and and_163 (and_163_out, undriven_14, undriven_6);
  and and_164 (and_164_out, or_1_out, undriven_15);
  and and_165 (and_165_out, undriven_15, undriven_7);
  and and_166 (and_166_out, or_1_out, undriven_16);
  and and_167 (and_167_out, undriven_16, undriven_8);
  and and_168 (and_168_out, or_1_out, undriven_17);
  and and_169 (and_169_out, undriven_17, undriven_9);
  and and_170 (and_170_out, or_1_out, undriven_18);
  and and_171 (and_171_out, undriven_18, undriven_10);
  and and_172 (and_172_out, or_1_out, undriven_19);
  and and_173 (and_173_out, undriven_19, undriven_11);
  and and_174 (and_174_out, or_1_out, undriven_20);
  and and_175 (and_175_out, undriven_20, undriven_12);
  S_R_Flip_Flop s_r_ff_73 (.Q(or_1_out), .reset(and_161_out), .preset(and_160_out));  // open: S, R, clk, Qn
  S_R_Flip_Flop s_r_ff_74 (.Q(or_1_out), .reset(and_163_out), .preset(and_162_out));  // open: S, R, clk, Qn
  S_R_Flip_Flop s_r_ff_75 (.Q(or_1_out), .reset(and_165_out), .preset(and_164_out));  // open: S, R, clk, Qn
  S_R_Flip_Flop s_r_ff_76 (.Q(or_1_out), .reset(and_167_out), .preset(and_166_out));  // open: S, R, clk, Qn
  S_R_Flip_Flop s_r_ff_77 (.Q(or_1_out), .reset(and_169_out), .preset(and_168_out));  // open: S, R, clk, Qn
  S_R_Flip_Flop s_r_ff_78 (.Q(or_1_out), .reset(and_171_out), .preset(and_170_out));  // open: S, R, clk, Qn
  S_R_Flip_Flop s_r_ff_79 (.Q(or_1_out), .reset(and_173_out), .preset(and_172_out));  // open: S, R, clk, Qn
  S_R_Flip_Flop s_r_ff_80 (.Q(or_1_out), .reset(and_175_out), .preset(and_174_out));  // open: S, R, clk, Qn

  // Notes on the sheet:
  //   8 bit Buffer - A
  //   8 bit Buffer - B
  //   S
  //   E
  //   R
  //   S
  //   E
  //   R
  //   Q
  //   Q
  //   B7
  //   S
  //   E
  //   R
  //   S
  //   E
  //   R
  //   B
  //   A
  //   A7
  //   Sum
  //   Carry IN
  //   Q
  //   B6
  //   Q
  //   Carry OUT
  //   S
  //   B
  //   A
  //   A6
  //   E
  //   R
  //   S
  //   E
  //   R
  //   Sum
  //   Carry IN
  //   Q
  //   Carry OUT
  //   B5
  //   Q
  //   A
  //   A5
  //   S
  //   E
  //   R
  //   B
  //   S
  //   E
  //   R
  //   Sum
  //   Carry IN
  //   Carry OUT
  //   Q
  //   A
  //   A4
  //   B4
  //   Q
  //   Sum
  //   B
  //   S
  //   E
  //   R
  //   S
  //   Carry IN
  //   E
  //   R
  //   Carry OUT
  //   8 bit Adder with carry
  //   A
  //   A3
  //   Q
  //   Q
  //   Sum
  //   B
  //   B3
  //   Carry IN
  //   Carry OUT
  //   S
  //   E
  //   R
  //   S
  //   E
  //   R
  //   A
  //   A2
  //   Sum
  //   B
  //   Carry IN
  //   Q
  //   B2
  //   Q
  //   Carry OUT
  //   S
  //   A
  //   E
  //   R
  //   S
  //   E
  //   R
  //   B
  //   A1
  //   Sum
  //   Carry IN
  //   Q
  //   Carry OUT
  //   B1
  //   Q
  //   S
  //   E
  //   R
  //   Sum
  //   A0
  //   S
  //   E
  //   R
  //   Carry
  //   Q
  //   B0
  //   Q
  //   RESET
  //   ENABLE
  //   RESET
  //   ENABLE
  //   A0
  //   A0
  //   A0
  //   A1
  //   A1
  //   A1
  //   A2
  //   A2
  //   A2
  //   A3
  //   A3
  //   A3
  //   Data Bus
  //   A4
  //   A4
  //   A4
  //   A5
  //   A5
  //   A5
  //   A6
  //   A6
  //   A6
  //   A7
  //   A7
  //   A7
  //   A8 (Carry Bit)
  //   A8 (Carry Bit)
  //   A8 (Carry Bit)
  //   S
  //   S
  //   S
  //   S
  //   S
  //   S
  //   S
  //   S
  //   E
  //   R
  //   E
  //   R
  //   E
  //   R
  //   E
  //   R
  //   E
  //   R
  //   E
  //   R
  //   E
  //   R
  //   E
  //   R
  //   Q
  //   Q
  //   Q
  //   Q
  //   Q
  //   Q
  //   Q
  //   Q
  //   S
  //   E
  //   R
  //   S
  //   E
  //   R
  //   S
  //   E
  //   R
  //   S
  //   E
  //   R
  //   S
  //   E
  //   R
  //   S
  //   E
  //   R
  //   S
  //   E
  //   R
  //   S
  //   E
  //   R
  //   Q
  //   Q
  //   Q
  //   Q
  //   Q
  //   Q
  //   Q
  //   Q
  //   S
  //   E
  //   R
  //   S
  //   E
  //   R
  //   S
  //   E
  //   R
  //   S
  //   E
  //   R
  //   S
  //   E
  //   R
  //   S
  //   E
  //   R
  //   S
  //   E
  //   R
  //   S
  //   E
  //   R
  //   Q
  //   Q
  //   Q
  //   Q
  //   Q
  //   Q
  //   Q
  //   Q
  //   S
  //   E
  //   R
  //   S
  //   E
  //   R
  //   S
  //   E
  //   R
  //   S
  //   E
  //   R
  //   S
  //   E
  //   R
  //   S
  //   E
  //   R
  //   S
  //   E
  //   R
  //   S
  //   E
  //   R
  //   Q
  //   Q
  //   Q
  //   Q
  //   Q
  //   Q
  //   Q
  //   Q
  //   S
  //   S
  //   S
  //   S
  //   S
  //   S
  //   S
  //   S
  //   E
  //   R
  //   E
  //   R
  //   E
  //   R
  //   E
  //   R
  //   E
  //   R
  //   E
  //   R
  //   E
  //   R
  //   E
  //   R
  //   Q
  //   Q
  //   Q
  //   Q
  //   Q
  //   Q
  //   Q
  //   Q
  //   S
  //   E
  //   R
  //   S
  //   E
  //   R
  //   S
  //   E
  //   R
  //   S
  //   E
  //   R
  //   S
  //   E
  //   R
  //   S
  //   E
  //   R
  //   S
  //   E
  //   R
  //   S
  //   E
  //   R
  //   Q
  //   Q
  //   Q
  //   Q
  //   Q
  //   Q
  //   Q
  //   Q
  //   S
  //   E
  //   R
  //   S
  //   E
  //   R
  //   S
  //   E
  //   R
  //   S
  //   E
  //   R
  //   S
  //   E
  //   R
  //   S
  //   E
  //   R
  //   S
  //   E
  //   R
  //   S
  //   E
  //   R
  //   Q
  //   Q
  //   Q
  //   Q
  //   Q
  //   Q
  //   Q
  //   Q
  //   S
  //   E
  //   R
  //   S
  //   E
  //   R
  //   S
  //   E
  //   R
  //   S
  //   E
  //   R
  //   S
  //   E
  //   R
  //   S
  //   E
  //   R
  //   S
  //   E
  //   R
  //   S
  //   E
  //   R
  //   Q
  //   Q
  //   Q
  //   Q
  //   Q
  //   Q
  //   Q
  //   Q
  //   RESET
  //   ENABLE
  //   RESET
  //   ENABLE
  //   RESET
  //   ENABLE
  //   RESET
  //   ENABLE
  //   RESET
  //   ENABLE
  //   RESET
  //   ENABLE
  //   RESET
  //   ENABLE
  //   RESET
  //   ENABLE
  //   Register A
  //   Register B
  //   Register C
  //   Register D
  //   Register E
  //   Register F
  //   Register G
  //   Register H
endmodule
